# Fritzing sketch fritzing (saved by Fritzing 0.9.3b)
breadboards: 1

parts:
  Arduino1 = Arduino Uno (Rev3)
  LED1 = LED - 5mm [color="Red (633nm)" package="5 mm [THT]"]
  LED2 = LED - 5mm [color="Red (633nm)" package="5 mm [THT]"]
  LED3 = LED - 5mm [color="Red (633nm)" package="5 mm [THT]"]
  LED4 = LED - 5mm [color="Red (633nm)" package="5 mm [THT]"]
  LED5 = LED - 5mm [color="Blue (430nm)" package="5 mm [THT]"]
  LED6 = LED - 5mm [color="Blue (430nm)" package="5 mm [THT]"]
  LED7 = LED - 5mm [color="Blue (430nm)" package="5 mm [THT]"]
  LED8 = LED - 5mm [color="Blue (430nm)" package="5 mm [THT]"]
  Q2 = NPN-Transistor [package="TO92 [THT]"]
  R1 = Resistor [tolerance=±5% resistance=220 package=THT]
  R2 = Resistor [tolerance=±5% resistance=220 package=THT]
  R3 = Resistor [tolerance=±5% resistance=220 package=THT]
  R4 = Resistor [tolerance=±5% resistance=220 package=THT]
  R5 = Resistor [tolerance=±5% resistance=10k package=THT]
  R6 = Resistor [tolerance=±5% resistance=10k package=THT]
  Q3 = NPN-Transistor [package="TO92 [THT]"]

nets:
  N1: Arduino1.D12/MISO, R6.Pin_1
  N2: Arduino1.D13/SCK, R5.Pin_1
  N3: Arduino1.GND, Q2.E, Q3.E
  N4: Arduino1.D1/TX, R4.Pin_1
  N5: Arduino1.D2, R3.Pin_1
  N6: Arduino1.D3_PWM, R2.Pin_1
  N7: Arduino1.D4, R1.Pin_1
  N8: LED1.cathode, LED2.cathode, LED3.cathode, LED4.cathode, Q2.C
  N9: LED1.anode, LED6.anode, R4.Pin_0
  N10: LED2.anode, LED8.anode, R1.Pin_0
  N11: LED4.anode, LED7.anode, R2.Pin_0
  N12: LED5.cathode, LED6.cathode, LED7.cathode, LED8.cathode, Q3.C
  N13: LED5.anode, R3.Pin_0
  N14: Q2.B, R5.Pin_0
  N15: R6.Pin_0, Q3.B
