# Fritzing sketch 05-fritzing (saved by Fritzing 0.9.3b)
breadboards: 1

parts:
  Arduino1 = Arduino Uno (Rev3)
  LED1 = LED - 5mm [color="White (4500K)" package="5 mm [THT]"]
  LED2 = LED - 5mm [color="White (4500K)" package="5 mm [THT]"]
  LED3 = LED - 5mm [color="White (4500K)" package="5 mm [THT]"]
  R1 = Resistor [tolerance=±5% resistance=100 package=THT]
  R4 = Resistor [tolerance=±5% resistance=100 package=THT]
  R5 = Resistor [tolerance=±5% resistance=100 package=THT]
  T1 = LM35 Temperature Sensor [package="TO92 [THT]"]

nets:
  N1: Arduino1.A0, T1.Vout
  N2: Arduino1.D11_PWM/MOSI, LED3.anode
  N3: Arduino1.D12/MISO, LED2.anode
  N4: Arduino1.D13/SCK, LED1.anode
  GND: Arduino1.GND, R1.Pin_0, R4.Pin_0, T1.GND
  N5: Arduino1.5V, T1.+Vs
  N6: LED1.cathode, R1.Pin_1
  N7: LED2.cathode, R4.Pin_1
  N8: LED3.cathode, R5.Pin_1
