# Fritzing sketch 03-fritzing (saved by Fritzing 0.9.3b)
breadboards: 1

parts:
  Arduino1 = Arduino Uno (Rev3)
  R1 = Resistor [tolerance=±5% resistance=220 package=THT]
  R2 = Resistor [tolerance=±5% resistance=100 package=THT]
  R3 = Resistor [tolerance=±5% resistance=100 package=THT]
  LED2 = RGB LED (com. cathode, rgb) [package="5 mm [THT]"]  # not connected

nets:
  N1: Arduino1.D9_PWM, R1.Pin_0
  N2: Arduino1.D5_PWM, R3.Pin_1
  N3: Arduino1.D6_PWM, R2.Pin_1
